# Fritzing sketch Schematics (saved by Fritzing 0.9.3b)

parts:
  WeMos_D1_Mini1 = WeMos D1 Mini
  BREAKOUT1 = ULN2003A breakout board
  MOTOR1 = 28BYJ-48 Stepper Motor
  S1 = Round Pushbutton
  S2 = Round Pushbutton
  J1 = Power Jack [package=power_jack_pth_lock]

nets:
  5V: WeMos_D1_Mini1.5V, BREAKOUT1.+5V, J1.GNDBREAK
  N1: WeMos_D1_Mini1.D1, BREAKOUT1.In_1
  N2: WeMos_D1_Mini1.D2, BREAKOUT1.In_2
  N3: WeMos_D1_Mini1.D3, BREAKOUT1.In_3
  N4: WeMos_D1_Mini1.D4, BREAKOUT1.In_4
  N5: WeMos_D1_Mini1.D6, S1.leg0
  N6: WeMos_D1_Mini1.D7, S2.leg0
  N7: WeMos_D1_Mini1.G, BREAKOUT1.0V, J1.GND
  N8: BREAKOUT1.RED_wire, MOTOR1.RED
  N9: BREAKOUT1.ORANGE_wire, MOTOR1.ORANGE
  N10: BREAKOUT1.YELLOW_wire, MOTOR1.YELLOW
  N11: BREAKOUT1.PINK_wire, MOTOR1.PINK
  N12: BREAKOUT1.BLUE_wire, MOTOR1.BLUE

notes:
  5V Supply

custom parts:
  ULN2003A breakout board: ULN2003A 7-way Darlington Transistor Driver on breakoutboard
